# Fritzing sketch Schéma final (saved by Fritzing 0.9.3b)
breadboards: 1

parts:
  Composant1 = Arduino Mega 2560 (Rev3)
  SP1 = SPEAKER [package=pcb_mount_speaker]  # not connected
  SP2 = SPEAKER [package=pcb_mount_speaker]  # not connected
  J1 = Basic Servo
  J2 = Basic Servo  # not connected
  LED1 = LEDs [package=fkit-led-1206]  # not connected
  LED2 = LEDs [package=fkit-led-1206]  # not connected
  LED3 = LEDs [package=fkit-led-1206]  # not connected
  LED4 = LEDs [package=fkit-led-1206]  # not connected
  LED5 = LEDs [package=fkit-led-1206]  # not connected
  LED6 = LEDs [package=fkit-led-1206]  # not connected
  S1 = Round Pushbutton
  VCC1 = Battery  # not connected
  BAT1 = BC9VPC [package=bc9vpc]
  microSD1 = MicroSD Card Module  # not connected

nets:
  N1: Composant1.GND, S1.leg1
  5V: Composant1.5V, J1.vcc, BAT1.V+
